// Logisim project CPU.circ as structural Verilog: 1 circuit, main circuit main
module main (
);

  wire and_1_out, and_2_out, and_3_out, and_4_out, and_5_out, button_1_out, clock_1_out, decoder_1_out0,
       decoder_1_out1, decoder_1_out2, decoder_1_out3, not_1_out, or_1_out;
  wire [1:0] ram_1_dout, ram_1_dout_3, ram_1_dout_4;
  wire [7:0] adder_1_out, adder_2_out, multiplexer_1_out, multiplexer_2_out, multiplexer_3_out,
       multiplexer_4_out, multiplier_1_out, PC_q, R0_q, R1_q, R2_q, R3_q, ram_2_dout;
  wire [7:6] ram_1_dout_2;

  Clock clock_1 (.out(clock_1_out));
  Button button_1 (.out(button_1_out));
  and and_1 (and_1_out, ram_1_dout_2[6], ram_1_dout_2[7]);
  or or_1 (or_1_out, clock_1_out, button_1_out);
  not not_1 (not_1_out, and_1_out);
  Decoder #(.select(2)) decoder_1 (
    .out0(decoder_1_out0), .out1(decoder_1_out1), .out2(decoder_1_out2), .out3(decoder_1_out3),
    .sel(ram_1_dout));  // open: en
  Register PC (.D(adder_1_out), .en(1'b1), .clk(or_1_out), .Q(PC_q));  // open: clr
  and and_2 (and_2_out, decoder_1_out0, not_1_out);
  and and_3 (and_3_out, decoder_1_out1, not_1_out);
  and and_4 (and_4_out, decoder_1_out2, not_1_out);
  and and_5 (and_5_out, decoder_1_out3, not_1_out);
  RAM #(.enables("line")) ram_1 (
    .addr(PC_q), .we(1'b0), .clk(or_1_out), .dout({ram_1_dout_2, ram_1_dout, ram_1_dout_4, ram_1_dout_3}));  // open: din
  Adder adder_1 (.a(PC_q), .b(8'h1), .out(adder_1_out));  // open: cin, cout
  Register R0 (.D(multiplexer_3_out), .en(and_2_out), .clk(or_1_out), .Q(R0_q));  // open: clr
  Register R1 (.D(multiplexer_3_out), .en(and_3_out), .clk(or_1_out), .Q(R1_q));  // open: clr
  Register R2 (.D(multiplexer_3_out), .en(and_4_out), .clk(or_1_out), .Q(R2_q));  // open: clr
  Register R3 (.D(multiplexer_3_out), .en(and_5_out), .clk(or_1_out), .Q(R3_q));  // open: clr
  Multiplexer #(.select(2), .width(8)) multiplexer_1 (
    .in0(R0_q), .in1(R1_q), .in2(R2_q), .in3(R3_q), .out(multiplexer_1_out), .sel(ram_1_dout_4));
  Multiplexer #(.select(2), .width(8)) multiplexer_2 (
    .in0(R0_q), .in1(R1_q), .in2(R2_q), .in3(R3_q), .out(multiplexer_2_out), .sel(ram_1_dout_3));
  Multiplexer #(.width(8)) multiplexer_3 (
    .in0(multiplexer_4_out), .in1(ram_2_dout), .out(multiplexer_3_out), .sel(ram_1_dout_2[7]));
  Adder adder_2 (.a(multiplexer_1_out), .b(multiplexer_2_out), .out(adder_2_out));  // open: cin, cout
  Multiplier multiplier_1 (.a(multiplexer_1_out), .b(multiplexer_2_out), .out(multiplier_1_out));  // open: cin, cout
  Multiplexer #(.width(8)) multiplexer_4 (
    .in0(adder_2_out), .in1(multiplier_1_out), .out(multiplexer_4_out), .sel(ram_1_dout_2[6]));
  RAM #(.addrWidth(4), .enables("line")) ram_2 (
    .addr({ram_1_dout_4, ram_1_dout_3}), .we(and_1_out), .clk(or_1_out), .din(multiplexer_1_out),
    .dout(ram_2_dout));

  // Notes on the sheet:
  //   Click the button to progress one clock cycle
  //   Else, click the clock to progress half a cycle
  //   The Clock
  //   Program Counter
  //   Instruction Memory
  //   Register File
  //   Name of CPU: Y8-ProtoMav
  //   Author: Orest Shkaba
  //   Adder
  //   ALU
  //   Multiplier
  //   Data Memory
endmodule
